# Fritzing sketch Rubik's Cube Solver - Stepper Motor Board (saved by Fritzing 0.9.4)
breadboards: 2

parts:
  Part1 = Arduino Uno (Rev3)  # not connected
  Power_plug1 = Power plug
  M3 = Stepper Motor - Bipolar  # not connected
  M4 = Stepper Motor - Bipolar  # not connected
  M5 = Stepper Motor - Bipolar  # not connected
  M6 = Stepper Motor - Bipolar  # not connected
  Raspberry_Pi_1 = Raspberry Pi 3 [part_number=RPI-3-V1.2]  # not connected
  M7 = Stepper Motor - Bipolar  # not connected
  DRV_7 = DRV 8825 Stepper Motor Carrier, High Current [part_number="DRV 8825"]  # not connected
  DRV_8 = DRV 8825 Stepper Motor Carrier, High Current [part_number="DRV 8825"]  # not connected
  C8 = Electrolytic Capacitor [capacitance=100µF voltage=50V package="200 mil [THT, electrolytic]"]
  DRV_9 = DRV 8825 Stepper Motor Carrier, High Current [part_number="DRV 8825"]  # not connected
  DRV_10 = DRV 8825 Stepper Motor Carrier, High Current [part_number="DRV 8825"]  # not connected
  DRV_11 = DRV 8825 Stepper Motor Carrier, High Current [part_number="DRV 8825"]  # not connected
  DRV_12 = DRV 8825 Stepper Motor Carrier, High Current [part_number="DRV 8825"]  # not connected
  C13 = Electrolytic Capacitor [capacitance=100µF voltage=50V package="200 mil [THT, electrolytic]"]
  C14 = Electrolytic Capacitor [capacitance=100µF voltage=50V package="200 mil [THT, electrolytic]"]
  C15 = Electrolytic Capacitor [capacitance=100µF voltage=50V package="200 mil [THT, electrolytic]"]
  C16 = Electrolytic Capacitor [capacitance=100µF voltage=50V package="200 mil [THT, electrolytic]"]
  C17 = Electrolytic Capacitor [capacitance=100µF voltage=50V package="200 mil [THT, electrolytic]"]
  M8 = Stepper Motor - Bipolar  # not connected

nets:
  N1: Power_plug1.GND, C8.-, C13.-, C14.-, C15.-, C16.-, C17.-
  N2: Power_plug1.VCC, C8.+, C13.+, C14.+, C15.+, C16.+, C17.+

// code stored in the sketch: Untitled.ino

